# Fritzing sketch pltn_range_sensor (saved by Fritzing 0.7.11b)
breadboards: 1

parts:
  Arduino1 = Arduino  # not connected
  Arduino_Ethernet_Shield1 = Arduino Ethernet Shield
  J1 = Infrared Proximity Sensor [part_number=SEN136B5B]
  LCD1 = LCD screen  # not connected

nets:
  N1: Arduino_Ethernet_Shield1.D2, J1.Vcc
  N2: Arduino_Ethernet_Shield1.+5V, J1.Vout
  GND: Arduino_Ethernet_Shield1.GND, J1.GND
